// Logisim project logic_diagram.circ as structural Verilog: 1 circuit, main circuit main
module main (
);

  wire adder_1_out, adder_2_cout, adder_2_out, adder_3_cout, adder_3_out, dipswitch_1_sw1, dipswitch_1_sw2,
       dipswitch_1_sw3, dipswitch_1_sw4, xor_1_out, xor_2_out, xor_3_out, xor_4_out;

  DipSwitch #(.number(4)) dipswitch_1 (
    .sw1(dipswitch_1_sw1), .sw2(dipswitch_1_sw2), .sw3(dipswitch_1_sw3), .sw4(dipswitch_1_sw4));
  xor xor_1 (xor_1_out, dipswitch_1_sw1, dipswitch_1_sw1);
  xor xor_2 (xor_2_out, dipswitch_1_sw1, dipswitch_1_sw2);
  Adder #(.width(1)) adder_1 (.a(1'b0), .b(xor_2_out), .out(adder_1_out), .cin(adder_2_cout));  // open: cout
  xor xor_3 (xor_3_out, dipswitch_1_sw1, dipswitch_1_sw3);
  xor xor_4 (xor_4_out, dipswitch_1_sw1, dipswitch_1_sw4);
  Adder #(.width(1)) adder_2 (.a(1'b0), .b(xor_3_out), .out(adder_2_out), .cin(adder_3_cout), .cout(adder_2_cout));
  Adder #(.width(1)) adder_3 (.a(1'b0), .b(xor_4_out), .out(adder_3_out), .cin(dipswitch_1_sw1), .cout(adder_3_cout));
endmodule
